// Logisim project cpu.circ as structural Verilog: 2 circuits, main circuit main
module main (
  input  [31:0] INSTRUCTION,
  input  CLOCK,
  output [31:0] PROGRAM_COUNTER,
  output [31:0] ra,
  output [31:0] sp,
  output [31:0] t0,
  output [31:0] t1,
  output [31:0] t2,
  output [31:0] s0,
  output [31:0] s1,
  output [31:0] a0
);

  wire ALUB, and_14_out, and_15_out, comparator_1_eq, comparator_2_eq, comparator_3_eq, comparator_4_eq,
       comparator_5_eq, comparator_6_eq, comparator_7_eq, comparator_8_eq, comparator_9_eq, comparator_10_eq,
       comparator_11_eq, comparator_12_eq, comparator_13_eq, comparator_14_eq, comparator_15_eq,
       comparator_16_eq, comparator_17_eq, comparator_18_eq, comparator_19_eq, MemRW;
  wire [3:0] ALUSel, ALUSelR, and_1_out, and_2_out, and_3_out, and_4_out, and_5_out, and_6_out, and_7_out,
       and_8_out, and_9_out, and_10_out, and_11_out, and_12_out, and_13_out, and_16_out, and_17_out,
       bit_extender_1_out, bit_extender_2_out, bit_extender_3_out, bit_extender_4_out, bit_extender_5_out,
       bit_extender_6_out, bit_extender_7_out, bit_extender_8_out, bit_extender_9_out, bit_extender_10_out,
       bit_extender_11_out, bit_extender_12_out, bit_extender_13_out, bit_extender_14_out,
       bit_extender_15_out;
  wire [4:0] rd_IF;
  wire [31:0] adder_1_out, alu_result, immi, multiplexer_1_out, multiplexer_2_out, multiplexer_3_out,
       multiplexer_4_out, Read_data, rs1_output, rs2_output, write_reg;

  imme imme_1 (.out_2(immi), .in_1(INSTRUCTION));
  Multiplexer #(.width(32), .enable("false")) multiplexer_1 (
    .in0(Read_data), .in1(alu_result), .out(multiplexer_1_out), .sel(1'b1));
  Register #(.width(5)) register_1 (.D(INSTRUCTION[11:7]), .en(1'b1), .clk(CLOCK), .Q(rd_IF));  // open: clr
  Comparator #(.width(5)) comparator_1 (
    .a({INSTRUCTION[14:12], INSTRUCTION[30], INSTRUCTION[25]}), .b(5'b01101), .eq(comparator_1_eq));  // open: gt, lt
  Comparator #(.width(5)) comparator_2 (
    .a({INSTRUCTION[14:12], INSTRUCTION[30], INSTRUCTION[25]}), .b({5{1'b0}}), .eq(comparator_2_eq));  // open: gt, lt
  Comparator #(.width(5)) comparator_3 (
    .a({INSTRUCTION[14:12], INSTRUCTION[30], INSTRUCTION[25]}), .b(5'b00001), .eq(comparator_3_eq));  // open: gt, lt
  Comparator #(.width(5)) comparator_4 (
    .a({INSTRUCTION[14:12], INSTRUCTION[30], INSTRUCTION[25]}), .b(5'b00010), .eq(comparator_4_eq));  // open: gt, lt
  Comparator #(.width(5)) comparator_5 (
    .a({INSTRUCTION[14:12], INSTRUCTION[30], INSTRUCTION[25]}), .b(5'b00100), .eq(comparator_5_eq));  // open: gt, lt
  Comparator #(.width(5)) comparator_6 (
    .a({INSTRUCTION[14:12], INSTRUCTION[30], INSTRUCTION[25]}), .b(5'b00101), .eq(comparator_6_eq));  // open: gt, lt
  Comparator #(.width(5)) comparator_7 (
    .a({INSTRUCTION[14:12], INSTRUCTION[30], INSTRUCTION[25]}), .b(5'b01000), .eq(comparator_7_eq));  // open: gt, lt
  Comparator #(.width(5)) comparator_8 (
    .a({INSTRUCTION[14:12], INSTRUCTION[30], INSTRUCTION[25]}), .b(5'b10000), .eq(comparator_8_eq));  // open: gt, lt
  Comparator #(.width(5)) comparator_9 (
    .a({INSTRUCTION[14:12], INSTRUCTION[30], INSTRUCTION[25]}), .b(5'b10101), .eq(comparator_9_eq));  // open: gt, lt
  Comparator #(.width(5)) comparator_10 (
    .a({INSTRUCTION[14:12], INSTRUCTION[30], INSTRUCTION[25]}), .b(5'b10100), .eq(comparator_10_eq));  // open: gt, lt
  Comparator #(.width(5)) comparator_11 (
    .a({INSTRUCTION[14:12], INSTRUCTION[30], INSTRUCTION[25]}), .b(5'b11000), .eq(comparator_11_eq));  // open: gt, lt
  Comparator #(.width(5)) comparator_12 (
    .a({INSTRUCTION[14:12], INSTRUCTION[30], INSTRUCTION[25]}), .b(5'b11101), .eq(comparator_12_eq));  // open: gt, lt
  Comparator #(.width(5)) comparator_13 (
    .a({INSTRUCTION[14:12], INSTRUCTION[30], INSTRUCTION[25]}), .b(5'b11100), .eq(comparator_13_eq));  // open: gt, lt
  Adder #(.width(32)) adder_1 (.a(PROGRAM_COUNTER), .b(32'h4), .out(adder_1_out));  // open: cin, cout
  Register #(.width(32)) PC (.D(adder_1_out), .en(1'b1), .clk(CLOCK), .Q(PROGRAM_COUNTER));  // open: clr
  assign bit_extender_1_out = {{3{comparator_1_eq}}, comparator_1_eq};  // Bit_Extender bit_extender_1
  assign bit_extender_2_out = {{3{comparator_2_eq}}, comparator_2_eq};  // Bit_Extender bit_extender_2
  assign bit_extender_3_out = {{3{comparator_3_eq}}, comparator_3_eq};  // Bit_Extender bit_extender_3
  assign bit_extender_4_out = {{3{comparator_4_eq}}, comparator_4_eq};  // Bit_Extender bit_extender_4
  assign bit_extender_5_out = {{3{comparator_5_eq}}, comparator_5_eq};  // Bit_Extender bit_extender_5
  assign bit_extender_6_out = {{3{comparator_6_eq}}, comparator_6_eq};  // Bit_Extender bit_extender_6
  assign bit_extender_7_out = {{3{comparator_7_eq}}, comparator_7_eq};  // Bit_Extender bit_extender_7
  assign bit_extender_8_out = {{3{comparator_8_eq}}, comparator_8_eq};  // Bit_Extender bit_extender_8
  assign bit_extender_9_out = {{3{comparator_9_eq}}, comparator_9_eq};  // Bit_Extender bit_extender_9
  assign bit_extender_10_out = {{3{comparator_10_eq}}, comparator_10_eq};  // Bit_Extender bit_extender_10
  assign bit_extender_11_out = {{3{comparator_11_eq}}, comparator_11_eq};  // Bit_Extender bit_extender_11
  assign bit_extender_12_out = {{3{comparator_12_eq}}, comparator_12_eq};  // Bit_Extender bit_extender_12
  assign bit_extender_13_out = {{3{comparator_13_eq}}, comparator_13_eq};  // Bit_Extender bit_extender_13
  Register #(.width(32)) register_2 (.D(multiplexer_1_out), .en(1'b1), .clk(CLOCK), .Q(write_reg));  // open: clr
  assign and_1_out = bit_extender_1_out & 4'b1011;  // AND_Gate and_1, 4 bits wide
  assign and_2_out = bit_extender_2_out & 4'b0000;  // AND_Gate and_2, 4 bits wide
  assign and_3_out = bit_extender_3_out & 4'b1010;  // AND_Gate and_3, 4 bits wide
  assign and_4_out = bit_extender_4_out & 4'b1100;  // AND_Gate and_4, 4 bits wide
  assign and_5_out = bit_extender_5_out & 4'b0110;  // AND_Gate and_5, 4 bits wide
  assign and_6_out = bit_extender_6_out & 4'b1110;  // AND_Gate and_6, 4 bits wide
  assign and_7_out = bit_extender_7_out & 4'b0111;  // AND_Gate and_7, 4 bits wide
  assign and_8_out = bit_extender_8_out & 4'b0011;  // AND_Gate and_8, 4 bits wide
  assign and_9_out = bit_extender_9_out & 4'b1000;  // AND_Gate and_9, 4 bits wide
  assign and_10_out = bit_extender_10_out & 4'b0100;  // AND_Gate and_10, 4 bits wide
  assign and_11_out = bit_extender_11_out & 4'b0010;  // AND_Gate and_11, 4 bits wide
  assign and_12_out = bit_extender_12_out & 4'b1001;  // AND_Gate and_12, 4 bits wide
  assign and_13_out = bit_extender_13_out & 4'b0001;  // AND_Gate and_13, 4 bits wide
  assign ALUSelR = and_1_out | and_2_out | and_3_out | and_4_out | and_5_out | and_6_out | and_7_out | and_8_out | and_9_out | and_10_out | and_11_out | and_12_out | and_13_out;  // OR_Gate or_1, 4 bits wide
  regfile_main RegFile (
    .rs2(INSTRUCTION[24:20]), .rd(rd_IF), .Read_Data_1(rs1_output), .Read_Data_2(rs2_output), .ra(ra),
    .sp(sp), .t0(t0), .t1(t1), .t2(t2), .s0(s0), .s1(s1), .a0(a0), .rs1(INSTRUCTION[19:15]),
    .Write_Data(write_reg), .RegWEn(1'b1), .clk(CLOCK));
  Multiplexer #(.width(32), .enable("false")) multiplexer_2 (
    .in0(rs2_output), .in1(write_reg), .out(multiplexer_2_out), .sel(comparator_14_eq));
  Comparator #(.width(5)) comparator_14 (.a(INSTRUCTION[24:20]), .b(rd_IF), .eq(comparator_14_eq));  // open: gt, lt
  Comparator #(.width(5)) comparator_15 (.a(INSTRUCTION[19:15]), .b(rd_IF), .eq(comparator_15_eq));  // open: gt, lt
  Multiplexer #(.width(32), .enable("false")) multiplexer_3 (
    .in0(immi), .in1(multiplexer_2_out), .out(multiplexer_3_out), .sel(ALUB));
  Multiplexer #(.width(32), .enable("false")) multiplexer_4 (
    .in0(rs1_output), .in1(write_reg), .out(multiplexer_4_out), .sel(comparator_15_eq));
  alu Arithmetic_Logic_Unit (.Result(alu_result), .ALUSel(ALUSel), .A(multiplexer_4_out), .B(multiplexer_3_out));
  // mem_main DMEM: pin names not known; wires that end beside it: alu_result, rs2_output, CLOCK, 1'b0, MemRW, Read_data
  Comparator #(.width(7)) comparator_16 (.a(INSTRUCTION[6:0]), .b(7'b0110011), .eq(comparator_16_eq));  // open: gt, lt
  Comparator #(.width(7)) comparator_17 (.a(INSTRUCTION[6:0]), .b(7'b0010011), .eq(comparator_17_eq));  // open: gt, lt
  Comparator #(.width(7)) comparator_18 (.a(INSTRUCTION[6:0]), .b(7'b0110011), .eq(comparator_18_eq));  // open: gt, lt
  Comparator #(.width(7)) comparator_19 (.a(INSTRUCTION[6:0]), .b(7'b0010011), .eq(comparator_19_eq));  // open: gt, lt
  and and_14 (and_14_out, comparator_16_eq, 1'b1);
  and and_15 (and_15_out, comparator_17_eq, 1'b0);
  assign bit_extender_14_out = {{3{comparator_18_eq}}, comparator_18_eq};  // Bit_Extender bit_extender_14
  assign bit_extender_15_out = {{3{comparator_19_eq}}, comparator_19_eq};  // Bit_Extender bit_extender_15
  or or_2 (ALUB, and_14_out, and_15_out);
  assign and_16_out = bit_extender_14_out & ALUSelR;  // AND_Gate and_16, 4 bits wide
  assign and_17_out = bit_extender_15_out & 4'b0000;  // AND_Gate and_17, 4 bits wide
  assign ALUSel = and_16_out | and_17_out;  // OR_Gate or_3, 4 bits wide

  // Other names for the same wires on the sheet: funct7[6:0] = INSTRUCTION[31:25];
  //   SEL[4:0] = {INSTRUCTION[14:12], INSTRUCTION[30], INSTRUCTION[25]}; funct3[2:0] = INSTRUCTION[14:12];
  //   clk = CLOCK; opcode[6:0] = INSTRUCTION[6:0]; rd[4:0] = INSTRUCTION[11:7]; rs1[4:0] = INSTRUCTION[19:15];
  //   rs2[4:0] = INSTRUCTION[24:20]

  // Notes on the sheet:
  //   mulhu
  //   add
  //   mul
  //   sub
  //   sll
  //   mulh
  //   slt
  //   xor
  //   divu
  //   srl
  //   or
  //   remu
  //   and
  //   Output
  //   R型
  //   IMEM (do **NOT** move this)
  //   Inputs
  //   Inputs/Outputs for testing. Do **NOT** move these.
  //   It is OK to move the PC, RegFile, ALU, and MEM to wherever is most convenient for you when constructing your CPU, and to delete this text
endmodule

module imme (
  input  [31:0] in_1,
  output [31:0] out_2
);

  wire [31:11] I, S;
  wire [31:12] SB;
  wire [31:20] UJ;

  Multiplexer #(.width(21), .enable("false")) multiplexer_1 (
    .in0({21{1'b0}}), .in1({21{1'b1}}), .out(I), .sel(in_1[31]));
  Multiplexer #(.width(21), .enable("false")) multiplexer_2 (
    .in0({21{1'b0}}), .in1({21{1'b1}}), .out(S), .sel(in_1[31]));
  Multiplexer #(.width(20), .enable("false")) multiplexer_3 (
    .in0({20{1'b0}}), .in1({20{1'b1}}), .out(SB), .sel(in_1[31]));
  Multiplexer #(.width(12), .enable("false")) multiplexer_4 (
    .in0({12{1'b0}}), .in1({12{1'b1}}), .out(UJ), .sel(in_1[31]));
  Multiplexer #(.select(3), .width(32), .enable("false")) multiplexer_5 (
    .in0({I, in_1[30:20]}), .in1({S, in_1[30:25], in_1[11:7]}),
    .in3({SB, in_1[7], in_1[30:25], in_1[11:8], 1'b0}), .in5({in_1[31:12], {12{1'b0}}}),
    .in7({UJ, in_1[19:12], in_1[20], in_1[30:21], 1'b0}), .out(out_2), .sel({in_1[2], in_1[6:5]}));  // open: in2, in4, in6

  // Other names for the same wires on the sheet: INSTRUCTION[31:0] = in_1; immi[31:0] = out_2;
  //   S[10:0] = {in_1[30:25], in_1[11:7]}; SB[11:1] = {in_1[7], in_1[30:25], in_1[11:8]}; U[31:12] = in_1[31:12];
  //   I[10:0] = in_1[30:20]; UJ[19:1] = {in_1[19:12], in_1[20], in_1[30:21]}

  // Notes on the sheet:
  //   Output
  //   Inputs
endmodule
